# Fritzing sketch board (saved by Fritzing 0.9.3b)
circuit board: 6.3cm x 4cm
breadboards: 1

parts:
  RST = Pushbutton [package="[THT]"]
  R_SYNC = Resistor [tolerance=±5% resistance=220 package=THT]
  R_CLR = Resistor [tolerance=±5% resistance=220 package=THT]
  OLED = Grove OLED 128x96
  WeMos_D1_Mini1 = WeMos D1 Mini
  CLR = LED - 3mm [color="White (6500K)" package="3 mm [THT]"]
  SYNC = LED - 3mm [color="White (6500K)" package="3 mm [THT]"]

nets:
  N1: RST.Pin_1, RST.Pin_2, WeMos_D1_Mini1.D8
  N2: RST.Pin_3, RST.Pin_4, OLED.GND, WeMos_D1_Mini1.G, CLR.cathode, SYNC.cathode
  N3: R_SYNC.Pin_0, SYNC.anode
  N4: R_SYNC.Pin_1, WeMos_D1_Mini1.D3
  N5: R_CLR.Pin_0, CLR.anode
  N6: R_CLR.Pin_1, WeMos_D1_Mini1.D5
  VCC: OLED.VCC, WeMos_D1_Mini1.5V
  N7: OLED.SDA, WeMos_D1_Mini1.D2
  N8: OLED.SCL, WeMos_D1_Mini1.D1
