# Fritzing sketch board (saved by Fritzing 0.9.3b)
circuit board: 6.3cm x 3.9cm
breadboards: 1

parts:
  RST = Pushbutton [package="[THT]"]
  CLR = LED - 3mm [color="White (6500K)" package="3 mm [THT]"]
  SYNC = LED - 3mm [color="White (6500K)" package="3 mm [THT]"]
  R2_PJ = Resistor [tolerance=±5% resistance=10k package=THT]
  R1_PJ = Resistor [tolerance=±5% resistance=10k package=THT]
  R3_PJ = Resistor [tolerance=±5% resistance=330 package=THT]
  PJ-307 = Audio Jack (TRS) 3.5mm [package="4Ucon 08780 [THT]"]
  WeMos_D1_Mini1 = WeMos D1 Mini
  Power = KF301-2 [part_number=KF301-2 package="screwterminal-5mm 2 position"]
  OLED = OLED Mono 0.56 inch blue or white
  R_SYNC = Resistor [tolerance=±5% resistance=220 package=THT]
  R_CLR = Resistor [tolerance=±5% resistance=220 package=THT]
  C_PJ = Electrolytic Capacitor [capacitance=100µF voltage=16V package="100 mil [THT, electrolytic]"]

nets:
  N1: RST.Pin_1, RST.Pin_2, WeMos_D1_Mini1.D8
  GND: RST.Pin_3, RST.Pin_4, CLR.cathode, SYNC.cathode, R1_PJ.Pin_1, WeMos_D1_Mini1.G, Power.2, OLED.GND, C_PJ.+
  N2: CLR.anode, R_CLR.Pin_0
  N3: SYNC.anode, R_SYNC.Pin_0
  5V: R2_PJ.Pin_0, WeMos_D1_Mini1.5V, Power.1, OLED.VCC
  N4: R2_PJ.Pin_1, R1_PJ.Pin_0, R3_PJ.Pin_0, PJ-307.Sleeve, C_PJ.-
  N5: R3_PJ.Pin_1, PJ-307.Tip, WeMos_D1_Mini1.A0
  N6: WeMos_D1_Mini1.D1, OLED.SCL
  N7: WeMos_D1_Mini1.D2, OLED.SDA
  N8: WeMos_D1_Mini1.D3, R_SYNC.Pin_1
  N9: WeMos_D1_Mini1.D5, R_CLR.Pin_1

notes:
  Power supply: HCR-15-5 ~15€
  Disjoncteur Phase/Neutre 10A 1 module ~8€
  +
  -
  SDA
  SCL
  VCC
  GND

custom parts:
  KF301-2: KF301-3 is a 3 position screw terminal header block with male through hole PCB pins on 5mm spacing
  OLED Mono 0.56 inch blue or white: OLED, I2C 3.3V - 5V Blue and White text versions
